# Fritzing sketch RZL_UHR_LEDS (saved by Fritzing 0.9.2b)
circuit board: 8.46667cm x 5.64444cm
breadboards: 1

parts:
  LED1 = LED - 3mm [color="Red (633nm)" package="3 mm [THT]"]
  LED2 = LED - 3mm [color="Red (633nm)" package="3 mm [THT]"]
  LED3 = LED - 3mm [color="Red (633nm)" package="3 mm [THT]"]
  LED4 = LED - 3mm [color="Red (633nm)" package="3 mm [THT]"]
  LED5 = LED - 3mm [color="Red (633nm)" package="3 mm [THT]"]
  LED6 = LED - 3mm [color="Red (633nm)" package="3 mm [THT]"]
  LED7 = LED - 3mm [color="Red (633nm)" package="3 mm [THT]"]
  LED8 = LED - 3mm [color="Red (633nm)" package="3 mm [THT]"]
  LED9 = LED - 3mm [color="Red (633nm)" package="3 mm [THT]"]
  LED10 = LED - 3mm [color="Red (633nm)" package="3 mm [THT]"]
  LED11 = LED - 3mm [color="Red (633nm)" package="3 mm [THT]"]
  LED12 = LED - 3mm [color="Red (633nm)" package="3 mm [THT]"]
  LED13 = LED - 3mm [color="Red (633nm)" package="3 mm [THT]"]
  LED14 = LED - 3mm [color="Red (633nm)" package="3 mm [THT]"]
  LED15 = LED - 3mm [color="Red (633nm)" package="3 mm [THT]"]
  LED16 = LED - 3mm [color="Red (633nm)" package="3 mm [THT]"]
  LED17 = LED - 3mm [color="Red (633nm)" package="3 mm [THT]"]
  LED18 = LED - 3mm [color="Red (633nm)" package="3 mm [THT]"]
  LED19 = LED - 3mm [color="Red (633nm)" package="3 mm [THT]"]
  LED20 = LED - 3mm [color="Red (633nm)" package="3 mm [THT]"]
  LED21 = LED - 3mm [color="Red (633nm)" package="3 mm [THT]"]
  LED22 = LED - 3mm [color="Red (633nm)" package="3 mm [THT]"]
  LED23 = LED - 3mm [color="Red (633nm)" package="3 mm [THT]"]
  LED24 = LED - 3mm [color="Red (633nm)" package="3 mm [THT]"]
  LED25 = LED - 3mm [color="Red (633nm)" package="3 mm [THT]"]
  LED26 = LED - 3mm [color="Red (633nm)" package="3 mm [THT]"]
  LED27 = LED - 3mm [color="Red (633nm)" package="3 mm [THT]"]
  LED28 = LED - 3mm [color="Red (633nm)" package="3 mm [THT]"]
  Zeilen = Header 3 [package=jst-3-smd]
  Zeilen_2 = Header 3 [package=jst-3-smd]
  JP3 = Header 3 [package=jst-3-smd]
  Spalten = Header 3 [package=jst-3-smd]
  Spalten_2 = Header 3 [package=jst-3-smd]
  JP6 = Header 3 [package=jst-3-smd]

nets (from the schematic view):
  N1: LED1.cathode, Zeilen.1
  N2: LED1.anode, Spalten.3
  N3: LED2.cathode, LED3.cathode, LED4.cathode, LED5.cathode, Zeilen.2
  N4: LED2.anode, LED3.anode, LED4.anode, LED5.anode, Spalten.2
  N5: LED6.cathode, LED7.cathode, LED8.cathode, LED9.cathode, Zeilen.3
  N6: LED6.anode, LED7.anode, LED8.anode, LED9.anode, Spalten.1
  N7: LED10.cathode, LED11.cathode, LED12.cathode, LED13.cathode, LED14.cathode, LED15.cathode, LED16.cathode, Zeilen_2.2
  N8: LED10.anode, LED11.anode, LED12.anode, LED13.anode, LED14.anode, LED15.anode, LED16.anode, Spalten_2.2
  N9: LED17.cathode, LED18.cathode, LED19.cathode, LED20.cathode, Zeilen_2.1
  N10: LED17.anode, LED18.anode, LED19.anode, LED20.anode, Spalten_2.3
  N11: LED21.cathode, LED22.cathode, LED23.cathode, LED24.cathode, Zeilen_2.3
  N12: LED21.anode, LED22.anode, LED23.anode, LED24.anode, Spalten_2.1
  N13: LED25.cathode, LED26.cathode, LED27.cathode, LED28.cathode, JP6.3
  N14: LED25.anode, LED26.anode, LED27.anode, LED28.anode, JP3.1
  N15: JP3.2, JP3.3
  N16: JP6.1, JP6.2
