# Fritzing sketch RZL_UHR_Teil1 (saved by Fritzing 0.9.2b)
circuit board: 12.8082cm x 5.91864cm
breadboards: 1

parts:
  LED1 = LED - 3mm [color="Red (633nm)" package="3 mm [THT]"]
  LED2 = LED - 3mm [color="Red (633nm)" package="3 mm [THT]"]
  LED3 = LED - 3mm [color="Red (633nm)" package="3 mm [THT]"]
  LED4 = LED - 3mm [color="Red (633nm)" package="3 mm [THT]"]
  LED5 = LED - 3mm [color="Red (633nm)" package="3 mm [THT]"]
  LED6 = LED - 3mm [color="Red (633nm)" package="3 mm [THT]"]
  LED7 = LED - 3mm [color="Red (633nm)" package="3 mm [THT]"]
  LED8 = LED - 3mm [color="Red (633nm)" package="3 mm [THT]"]
  LED9 = LED - 3mm [color="Red (633nm)" package="3 mm [THT]"]
  LED10 = LED - 3mm [color="Red (633nm)" package="3 mm [THT]"]
  LED11 = LED - 3mm [color="Red (633nm)" package="3 mm [THT]"]
  LED12 = LED - 3mm [color="Red (633nm)" package="3 mm [THT]"]
  LED13 = LED - 3mm [color="Red (633nm)" package="3 mm [THT]"]
  LED14 = LED - 3mm [color="Red (633nm)" package="3 mm [THT]"]
  LED15 = LED - 3mm [color="Red (633nm)" package="3 mm [THT]"]
  LED16 = LED - 3mm [color="Red (633nm)" package="3 mm [THT]"]
  LED17 = LED - 3mm [color="Red (633nm)" package="3 mm [THT]"]
  LED18 = LED - 3mm [color="Red (633nm)" package="3 mm [THT]"]
  LED19 = LED - 3mm [color="Red (633nm)" package="3 mm [THT]"]
  LED20 = LED - 3mm [color="Red (633nm)" package="3 mm [THT]"]
  LED21 = LED - 3mm [color="Red (633nm)" package="3 mm [THT]"]
  LED22 = LED - 3mm [color="Red (633nm)" package="3 mm [THT]"]
  LED23 = LED - 3mm [color="Red (633nm)" package="3 mm [THT]"]
  LED24 = LED - 3mm [color="Red (633nm)" package="3 mm [THT]"]
  JP1 = Header 6 [package=1x06-smd]
  JP2 = Header 6 [package=1x06-smd]
  JP3 = Header 6 [package=1x06-smd]

nets:
  N1: LED1.cathode, JP3.1
  N2: LED1.anode, LED4.anode, LED6.anode, LED12.anode, LED19.anode, LED21.anode, JP1.2
  N3: LED2.cathode, LED3.cathode, LED4.cathode, LED5.cathode, JP3.2
  N4: LED2.anode, LED7.anode, LED13.anode, LED18.anode, LED22.anode, JP1.3
  N5: LED3.anode, LED8.anode, LED14.anode, LED17.anode, LED23.anode, JP1.4
  N6: LED5.anode, LED9.anode, LED15.anode, LED16.anode, LED24.anode, JP1.5
  N7: LED6.cathode, LED7.cathode, LED8.cathode, LED9.cathode, JP3.3
  N8: LED10.cathode, LED11.cathode, LED16.cathode, LED17.cathode, LED18.cathode, LED19.cathode, LED20.cathode, JP3.4
  N9: LED10.anode, JP1.6
  N10: LED11.anode, JP2.1
  N11: LED12.cathode, LED13.cathode, LED14.cathode, LED15.cathode, JP3.5
  N12: LED20.anode, JP1.1
  N13: LED21.cathode, LED22.cathode, LED23.cathode, LED24.cathode, JP3.6
