# Fritzing sketch RZL_Uhr_2 (saved by Fritzing 0.9.2b)
breadboards: 1

parts:
  LED1 = LED - 3mm [color="Red (633nm)" package="3 mm [THT]"]
  LED2 = LED - 3mm [color="Red (633nm)" package="3 mm [THT]"]
  LED3 = LED - 3mm [color="Red (633nm)" package="3 mm [THT]"]
  LED4 = LED - 3mm [color="Red (633nm)" package="3 mm [THT]"]
  LED5 = LED - 3mm [color="Red (633nm)" package="3 mm [THT]"]
  LED6 = LED - 3mm [color="Red (633nm)" package="3 mm [THT]"]
  LED7 = LED - 3mm [color="Red (633nm)" package="3 mm [THT]"]
  LED8 = LED - 3mm [color="Red (633nm)" package="3 mm [THT]"]
  LED9 = LED - 3mm [color="Red (633nm)" package="3 mm [THT]"]
  LED10 = LED - 3mm [color="Red (633nm)" package="3 mm [THT]"]
  LED11 = LED - 3mm [color="Red (633nm)" package="3 mm [THT]"]
  LED12 = LED - 3mm [color="Red (633nm)" package="3 mm [THT]"]
  LED13 = LED - 3mm [color="Red (633nm)" package="3 mm [THT]"]
  LED14 = LED - 3mm [color="Red (633nm)" package="3 mm [THT]"]
  LED15 = LED - 3mm [color="Red (633nm)" package="3 mm [THT]"]
  LED16 = LED - 3mm [color="Red (633nm)" package="3 mm [THT]"]
  LED17 = LED - 3mm [color="Red (633nm)" package="3 mm [THT]"]
  LED18 = LED - 3mm [color="Red (633nm)" package="3 mm [THT]"]
  LED19 = LED - 3mm [color="Red (633nm)" package="3 mm [THT]"]
  LED20 = LED - 3mm [color="Red (633nm)" package="3 mm [THT]"]
  LED21 = LED - 3mm [color="Red (633nm)" package="3 mm [THT]"]
  LED22 = LED - 3mm [color="Red (633nm)" package="3 mm [THT]"]
  LED23 = LED - 3mm [color="Red (633nm)" package="3 mm [THT]"]
  LED24 = LED - 3mm [color="Red (633nm)" package="3 mm [THT]"]
  JP1 = Header 3 [package=jst-3-pth]
  JP2 = Header 2 [package=jst-2-pth-kit]
  JP3 = Header 2 [package=jst-2-pth-kit]
  JP4 = Header 3 [package=jst-3-pth]
  JP5 = Header 2 [package=jst-2-pth-kit]

nets:
  N1: LED1.cathode, LED15.cathode, JP1.1
  N2: LED1.anode, LED2.anode, LED3.anode, LED4.anode, LED5.anode, JP5.1
  N3: LED2.cathode, LED6.cathode, LED13.cathode, LED14.cathode, LED21.cathode, JP2.2
  N4: LED3.cathode, LED7.cathode, LED11.cathode, LED16.cathode, LED22.cathode, JP2.1
  N5: LED4.cathode, LED8.cathode, LED10.cathode, LED18.cathode, LED23.cathode, JP3.2
  N6: LED5.cathode, LED9.cathode, LED12.cathode, LED20.cathode, LED24.cathode, JP3.1
  N7: LED6.anode, LED7.anode, LED8.anode, LED9.anode, JP5.2
  N8: LED10.anode, LED11.anode, LED12.anode, LED14.anode, LED15.anode, LED17.anode, LED19.anode, JP4.1
  N9: LED13.anode, LED16.anode, LED18.anode, LED20.anode, JP4.2
  N10: LED17.cathode, JP1.2
  N11: LED19.cathode, JP1.3
  N12: LED21.anode, LED22.anode, LED23.anode, LED24.anode, JP4.3
