# Fritzing sketch Uhr_Matrix_komplett (saved by Fritzing 0.9.2b)
breadboards: 1

parts:
  Dot_Matrix1 = LED Dot Matrix 18mm (0.7 INCH)
  U1 = MAX7219 [package=dil24]
  C1 = Capacitor [package=cap-pth-small-kit]
  C2 = Capacitor Polarized [package=panasonic_c]
  Bauteil1 = Arduino Uno (Rev3) - ICSP
  R1 = Resistor [tolerance=±5% resistance=33k package=THT]
  IC1 = DS3231MZ Real Time Clock
  S1 = Pushbutton [package="[THT]"]
  S2 = Pushbutton [package="[THT]"]

nets:
  N1: Dot_Matrix1.Column_1, Dot_Matrix1.Row_3
  N2: Dot_Matrix1.Row_6, Dot_Matrix1.Row_7
  N3: Dot_Matrix1.Column_4, Dot_Matrix1.Column_5, U1.SEGA
  N4: Dot_Matrix1.Row_2, Dot_Matrix1.Row_1, U1.DIG6
  N5: U1.DIN, Bauteil1.ICSP_MISO, Bauteil1.D12/MISO
  GND: U1.GND, U1.GND2
  N6: U1.LOAD, Bauteil1.D10_PWM/SS
  N7: U1.CLK, Bauteil1.ICSP_MOSI, Bauteil1.D11_PWM/MOSI
  N8: U1.ISET, R1.Pin_1
  VCC: U1.VCC, C2.-, Bauteil1.5V, R1.Pin_0, IC1.Pin_2
  N9: C1.1, C2.+
  N10: C1.2, Bauteil1.GND, IC1.Pin_5, S1.Pin_3, S1.Pin_4, S2.Pin_3, S2.Pin_4
  N11: Bauteil1.A4/SDA, IC1.Pin_7
  N12: Bauteil1.A5/SCL, IC1.Pin_8
  N13: Bauteil1.D2, S1.Pin_1, S1.Pin_2
  N14: Bauteil1.D3_PWM, S2.Pin_1, S2.Pin_2

custom parts:
  DS3231MZ Real Time Clock: DS3231MZ Real Time Clock. SO-8 surface mount version.
