# Fritzing sketch Uhr_Matrix_ohne_DS3231 (saved by Fritzing 0.9.2b)
breadboards: 1

parts:
  Dot_Matrix1 = LED Dot Matrix 18mm (0.7 INCH)
  U1 = MAX7219 [package=dil24]
  C1 = Capacitor [package=cap-pth-small-kit]
  C2 = Capacitor Polarized [package=panasonic_c]
  R1 = Resistor [tolerance=±5% resistance=33k package="2010 [SMD]"]
  Bauteil1 = Arduino Uno (Rev3) - ICSP

nets:
  N1: Dot_Matrix1.Column_1, Dot_Matrix1.Row_3
  N2: Dot_Matrix1.Row_6, Dot_Matrix1.Row_7
  N3: Dot_Matrix1.Column_4, Dot_Matrix1.Column_5, U1.SEGA
  N4: Dot_Matrix1.Row_2, Dot_Matrix1.Row_1, U1.DIG6
  N5: U1.DIN, Bauteil1.ICSP_MISO, Bauteil1.D12/MISO
  GND: U1.GND, U1.GND2
  N6: U1.LOAD, Bauteil1.D10_PWM/SS
  N7: U1.CLK, Bauteil1.ICSP_MOSI, Bauteil1.D11_PWM/MOSI
  N8: U1.ISET, R1.Pin_1
  VCC: U1.VCC, C2.-, R1.Pin_0, Bauteil1.5V
  N9: C1.1, C2.+
  N10: C1.2, Bauteil1.GND
